// Logisim project y86_processor.circ as structural Verilog: 7 circuits, main circuit main
module main (
);

  wire clock_1_out;
  wire [3:0] fetch_1_icode, fetch_1_ifun, fetch_1_ra, fetch_1_rb;
  wire [11:0] fetch_1_valp, Program_Counter_q;
  wire [63:0] fetch_1_valc;

  Clock clock_1 (.out(clock_1_out));
  Register #(.width(4)) icode (.D(fetch_1_icode), .clk(clock_1_out));  // open: en, Q, clr
  Register #(.width(4)) ifun (.D(fetch_1_ifun), .clk(clock_1_out));  // open: en, Q, clr
  Register #(.width(4)) rA (.D(fetch_1_ra), .clk(clock_1_out));  // open: en, Q, clr
  Register #(.width(12)) Program_Counter (.clk(clock_1_out), .Q(Program_Counter_q));  // open: D, en, clr
  Register #(.width(4)) rB (.D(fetch_1_rb), .clk(clock_1_out));  // open: en, Q, clr
  fetch fetch_1 (
    .clk(clock_1_out), .PC(Program_Counter_q), .icode(fetch_1_icode), .ifun(fetch_1_ifun), .rA(fetch_1_ra),
    .rB(fetch_1_rb), .valC(fetch_1_valc), .ValP(fetch_1_valp));
  Register #(.width(64)) ValC (.D(fetch_1_valc), .clk(clock_1_out));  // open: en, Q, clr
  Register #(.width(12)) ValP (.D(fetch_1_valp), .clk(clock_1_out));  // open: en, Q, clr

  // Notes on the sheet:
  //   account for the frequency of the clock by the worst case scenario of instruction (idk how to calculate)
endmodule

module fetch (
  input  clk,
  input  [11:0] PC,
  output [3:0] icode,
  output [3:0] ifun,
  output [3:0] rA,
  output [3:0] rB,
  output [63:0] valC,
  output [11:0] ValP
);

  wire need_regids_1_true, need_valc_1_true;
  wire [7:0] instruction_memory_1_byte1, instruction_memory_1_byte2, instruction_memory_1_byte3,
       instruction_memory_1_byte4, instruction_memory_1_byte5, instruction_memory_1_byte6,
       instruction_memory_1_byte7, instruction_memory_1_byte8, instruction_memory_1_byte9;

  Instruction_Memory instruction_memory_1 (
    .PC(PC), .clk(clk), .Byte0({ifun, icode}), .Byte1(instruction_memory_1_byte1),
    .Byte2(instruction_memory_1_byte2), .Byte3(instruction_memory_1_byte3),
    .Byte4(instruction_memory_1_byte4), .Byte5(instruction_memory_1_byte5),
    .Byte6(instruction_memory_1_byte6), .Byte7(instruction_memory_1_byte7),
    .Byte8(instruction_memory_1_byte8), .Byte9(instruction_memory_1_byte9));
  Need_valC need_valc_1 (.icode(icode), .true(need_valc_1_true));
  Need_regIDs need_regids_1 (.icode(icode), .true(need_regids_1_true));
  align align_1 (
    .icode(icode), .Byte1(instruction_memory_1_byte1), .Byte2(instruction_memory_1_byte2),
    .Byte3(instruction_memory_1_byte3), .Byte4(instruction_memory_1_byte4),
    .Byte5(instruction_memory_1_byte5), .Byte6(instruction_memory_1_byte6),
    .Byte7(instruction_memory_1_byte7), .Byte8(instruction_memory_1_byte8),
    .Byte9(instruction_memory_1_byte9), .rA(rA), .rB(rB), .valC(valC));
  PC_Increment pc_increment_1 (.Need_ValC(need_valc_1_true), .Need_RegIDs(need_regids_1_true), .PC(PC), .ValP(ValP));

  // Notes on the sheet:
  //   update PC_inc
  //   ValP = PC + 1 + Need_regIDs + Need_ValC * 8
endmodule

module Instruction_Memory (
  input  [11:0] PC,
  input  clk,
  output [7:0] Byte0,
  output [7:0] Byte1,
  output [7:0] Byte2,
  output [7:0] Byte3,
  output [7:0] Byte4,
  output [7:0] Byte5,
  output [7:0] Byte6,
  output [7:0] Byte7,
  output [7:0] Byte8,
  output [7:0] Byte9
);

  wire [3:0] counter_1_q;
  wire [7:0] ram_1_dout;
  wire [11:0] adder_1_out;

  Adder #(.width(12)) adder_1 (.a(PC), .b(12'h1), .out(adder_1_out));  // open: cin, cout
  RAM #(.addrWidth(12)) ram_1 (.addr(adder_1_out), .clk(clk), .dout(ram_1_dout));  // open: we, oe, din
  Counter #(.max('h9), .width(4)) counter_1 (.clk(clk), .Q(counter_1_q));  // open: clr, load, up, count, D, carry
  Demultiplexer #(.select(4), .width(8)) demultiplexer_1 (
    .out0(Byte0), .out1(Byte1), .out2(Byte2), .out3(Byte3), .out4(Byte4), .out5(Byte5), .out6(Byte6),
    .out7(Byte7), .out8(Byte8), .out9(Byte9), .in(ram_1_dout), .sel(counter_1_q));  // open: out10, out11, out12, out13, out14, out15
endmodule

module align (
  input  [3:0] icode,
  input  [7:0] Byte1,
  input  [7:0] Byte2,
  input  [7:0] Byte3,
  input  [7:0] Byte4,
  input  [7:0] Byte5,
  input  [7:0] Byte6,
  input  [7:0] Byte7,
  input  [7:0] Byte8,
  input  [7:0] Byte9,
  output [3:0] rA,
  output [3:0] rB,
  output [63:0] valC
);

  wire decoder_1_out3, decoder_1_out7, decoder_1_out8, decoder_1_out10, decoder_1_out11, or_1_out, or_2_out,
       or_3_out;

  Decoder #(.select(4)) decoder_1 (
    .out3(decoder_1_out3), .out7(decoder_1_out7), .out8(decoder_1_out8), .out10(decoder_1_out10),
    .out11(decoder_1_out11), .sel(icode));  // open: out0, out1, out2, out4, out5, out6, out9, out12, out13, out14, out15, en
  Multiplexer #(.width(4)) multiplexer_1 (.in0(Byte1[3:0]), .in1(4'b1111), .out(rA), .sel(or_1_out));
  or or_1 (or_1_out, decoder_1_out3, decoder_1_out7, decoder_1_out8);
  Multiplexer #(.width(4)) multiplexer_2 (.in0(Byte1[7:4]), .in1(4'b1111), .out(rB), .sel(or_2_out));
  or or_2 (or_2_out, decoder_1_out7, decoder_1_out8, decoder_1_out10, decoder_1_out11);
  Multiplexer #(.width(64)) multiplexer_3 (
    .in0({Byte9, Byte8, Byte7, Byte6, Byte5, Byte4, Byte3, Byte2}),
    .in1({Byte8, Byte7, Byte6, Byte5, Byte4, Byte3, Byte2, Byte1}), .out(valC), .sel(or_3_out));
  or or_3 (or_3_out, decoder_1_out7, decoder_1_out8);
endmodule

module Need_valC (
  input  [3:0] icode,
  output true
);

  wire decoder_1_out3, decoder_1_out4, decoder_1_out5, decoder_1_out7, decoder_1_out8;

  Decoder #(.select(4)) decoder_1 (
    .out3(decoder_1_out3), .out4(decoder_1_out4), .out5(decoder_1_out5), .out7(decoder_1_out7),
    .out8(decoder_1_out8), .sel(icode));  // open: out0, out1, out2, out6, out9, out10, out11, out12, out13, out14, out15, en
  or or_1 (true, decoder_1_out3, decoder_1_out4, decoder_1_out5, decoder_1_out7, decoder_1_out8);
endmodule

module Need_regIDs (
  input  [3:0] icode,
  output true
);

  wire decoder_1_out2, decoder_1_out3, decoder_1_out4, decoder_1_out5, decoder_1_out6, decoder_1_out10,
       decoder_1_out11;

  Decoder #(.select(4)) decoder_1 (
    .out2(decoder_1_out2), .out3(decoder_1_out3), .out4(decoder_1_out4), .out5(decoder_1_out5),
    .out6(decoder_1_out6), .out10(decoder_1_out10), .out11(decoder_1_out11), .sel(icode));  // open: out0, out1, out7, out8, out9, out12, out13, out14, out15, en
  or or_1 (true, decoder_1_out2, decoder_1_out3, decoder_1_out4, decoder_1_out5, decoder_1_out6, decoder_1_out10, decoder_1_out11);
endmodule

module PC_Increment (
  input  Need_ValC,
  input  Need_RegIDs,
  input  [11:0] PC,
  output [11:0] ValP
);

  wire [11:0] adder_1_out, adder_2_out, multiplexer_1_out, multiplexer_2_out;

  Multiplexer #(.width(12)) multiplexer_1 (.in0({12{1'b0}}), .in1(12'h1), .out(multiplexer_1_out), .sel(Need_RegIDs));
  Adder #(.width(12)) adder_1 (.a(12'h1), .b(PC), .out(adder_1_out));  // open: cin, cout
  Multiplexer #(.width(12)) multiplexer_2 (.in0({12{1'b0}}), .in1(12'h8), .out(multiplexer_2_out), .sel(Need_ValC));
  Adder #(.width(12)) adder_2 (.a(multiplexer_1_out), .b(adder_1_out), .out(adder_2_out));  // open: cin, cout
  Adder #(.width(12)) adder_3 (.a(multiplexer_2_out), .b(adder_2_out), .out(ValP));  // open: cin, cout
endmodule
